// Logisim project mockup.circ as structural Verilog: 10 circuits, main circuit alu
module main (
);

  wire idex_1_alu_in1_sel, idex_1_alu_in2_sel, idex_1_alu_mod, instr_decoder_1_alu_in1_sel,
       instr_decoder_1_alu_in2_sel, instr_decoder_1_alu_mod, instr_decoder_1_is_cond,
       instr_decoder_1_mem_mode, instr_decoder_1_nextpc_sel;
  wire [1:0] instr_decoder_1_rf_in_sel;
  wire [2:0] idex_1_alu_op, idex_1_funct3, instr_decoder_1_alu_op, instr_decoder_1_funct3;
  wire [4:0] instr_decoder_1_rread1, instr_decoder_1_rread2, instr_decoder_1_rwrite;
  wire [31:0] idex_1_imm, idex_1_pc, idex_1_reg1, idex_1_reg2, ifid_1_instr, ifid_1_pc, instr_decoder_1_imm,
       instr_mem_1_instr, multiplexer_1_out, multiplexer_2_out, pc_1_curpc, regfile_1_reg1_out,
       regfile_1_reg2_out;

  pc pc_1 (.curpc(pc_1_curpc));  // open: nextpc
  instr_mem instr_mem_1 (.addr(pc_1_curpc), .instr(instr_mem_1_instr));
  ifid ifid_1 (.instr_in(instr_mem_1_instr), .pc_in(pc_1_curpc), .instr(ifid_1_instr), .pc(ifid_1_pc));
  instr_decoder instr_decoder_1 (
    .instr(ifid_1_instr), .rread1(instr_decoder_1_rread1), .rread2(instr_decoder_1_rread2),
    .imm(instr_decoder_1_imm), .alu_in1_sel(instr_decoder_1_alu_in1_sel),
    .alu_in2_sel(instr_decoder_1_alu_in2_sel), .alu_op(instr_decoder_1_alu_op),
    .alu_mod(instr_decoder_1_alu_mod), .funct3(instr_decoder_1_funct3),
    .rf_in_sel(instr_decoder_1_rf_in_sel), .mem_mode(instr_decoder_1_mem_mode),
    .is_cond(instr_decoder_1_is_cond), .nextpc_sel(instr_decoder_1_nextpc_sel),
    .rwrite(instr_decoder_1_rwrite));
  regfile regfile_1 (
    .reg1_sel(instr_decoder_1_rread1), .reg2_sel(instr_decoder_1_rread2), .reg1_out(regfile_1_reg1_out),
    .reg2_out(regfile_1_reg2_out));  // open: write_sel, write_data
  Multiplexer #(.width(32)) multiplexer_1 (
    .in0(idex_1_reg1), .in1(idex_1_pc), .out(multiplexer_1_out), .sel(idex_1_alu_in1_sel));
  idex idex_1 (
    .rwrite_in(instr_decoder_1_rwrite), .imm_in(instr_decoder_1_imm),
    .alu_in1_sel_in(instr_decoder_1_alu_in1_sel), .alu_in2_sel_in(instr_decoder_1_alu_in2_sel),
    .pc_in(ifid_1_pc), .alu_op_in(instr_decoder_1_alu_op), .alu_mod_in(instr_decoder_1_alu_mod),
    .funct3_in(instr_decoder_1_funct3), .mem_mode_in(instr_decoder_1_mem_mode),
    .is_cond_in(instr_decoder_1_is_cond), .nextpc_sel_in(instr_decoder_1_nextpc_sel),
    .reg1_in(regfile_1_reg1_out), .reg2_in(regfile_1_reg2_out), .rf_in_sel_in(instr_decoder_1_rf_in_sel),
    .imm(idex_1_imm), .alu_in1_sel(idex_1_alu_in1_sel), .alu_in2_sel(idex_1_alu_in2_sel), .pc(idex_1_pc),
    .alu_op(idex_1_alu_op), .alu_mod(idex_1_alu_mod), .funct3(idex_1_funct3), .reg1(idex_1_reg1),
    .reg2(idex_1_reg2));  // open: rf_in_sel, mem_mode, is_cond, nextpc_sel, rwrite
  Multiplexer #(.width(32)) multiplexer_2 (
    .in0(idex_1_reg2), .in1(idex_1_imm), .out(multiplexer_2_out), .sel(idex_1_alu_in2_sel));
  alu alu_1 (
    .alu_in1(multiplexer_1_out), .alu_in2(multiplexer_2_out), .alu_op(idex_1_alu_op), .alu_mod(idex_1_alu_mod));  // open: alu_out
  compare compare_1 (.in1(idex_1_reg1), .in2(idex_1_reg2), .funct3(idex_1_funct3));  // open: res
endmodule

module alu (
  input  [31:0] alu_in1,
  input  [31:0] alu_in2,
  input  [2:0] alu_op,
  input  alu_mod,
  output [31:0] alu_out
);
endmodule

module data_mem (
  input  [31:0] addr,
  input  [31:0] write_data,
  input  mem_mode,
  output [31:0] mem_out
);
endmodule

module instr_decoder (
  input  [31:0] instr,
  output [4:0] rread1,
  output [4:0] rread2,
  output [31:0] imm,
  output alu_in1_sel,
  output alu_in2_sel,
  output [2:0] alu_op,
  output alu_mod,
  output [2:0] funct3,
  output [1:0] rf_in_sel,
  output mem_mode,
  output is_cond,
  output nextpc_sel,
  output [4:0] rwrite
);
endmodule

module instr_mem (
  input  [31:0] addr,
  output [31:0] instr
);
endmodule

module pc (
  input  [31:0] nextpc,
  output [31:0] curpc
);
endmodule

module regfile (
  input  [4:0] reg1_sel,
  input  [4:0] reg2_sel,
  input  [4:0] write_sel,
  input  [31:0] write_data,
  output [31:0] reg1_out,
  output [31:0] reg2_out
);
endmodule

module ifid (
  input  [31:0] pc_in,
  input  [31:0] instr_in,
  output [31:0] pc,
  output [31:0] instr
);
endmodule

module idex (
  input  [31:0] pc_in,
  input  [31:0] reg1_in,
  input  [31:0] reg2_in,
  input  [31:0] imm_in,
  input  alu_in1_sel_in,
  input  alu_in2_sel_in,
  input  [2:0] alu_op_in,
  input  alu_mod_in,
  input  [2:0] funct3_in,
  input  [1:0] rf_in_sel_in,
  input  mem_mode_in,
  input  is_cond_in,
  input  nextpc_sel_in,
  input  [4:0] rwrite_in,
  output [31:0] pc,
  output [31:0] reg1,
  output [31:0] reg2,
  output [31:0] imm,
  output alu_in1_sel,
  output alu_in2_sel,
  output [2:0] alu_op,
  output alu_mod,
  output [2:0] funct3,
  output [1:0] rf_in_sel,
  output mem_mode,
  output is_cond,
  output nextpc_sel,
  output [4:0] rwrite
);
endmodule

module compare (
  input  [31:0] in1,
  input  [31:0] in2,
  input  [2:0] funct3,
  output res
);
endmodule
