// Logisim project v1.circ as structural Verilog
module alu (
  input  [31:0] a,
  input  [31:0] b,
  input  [2:0] alu_op,
  output [31:0] alu_out
);
endmodule

module data_mem (
  input  [31:0] addr,
  input  [31:0] write_data,
  input  [2:0] funct3,
  input  mem_mode,
  output [31:0] mem_out
);
endmodule

module instr_decoder (
  input  [31:0] instr,
  output [4:0] rs1,
  output [4:0] rs2,
  output [31:0] imm,
  output alu_in1_sel,
  output alu_in2_sel,
  output [2:0] alu_op,
  output [2:0] funct3,
  output is_cond,
  output nextpc_sel,
  output mem_mode,
  output [1:0] rf_in_sel,
  output [4:0] rd
);
endmodule

module instr_mem (
  input  [31:0] addr,
  output [31:0] instr
);
endmodule

module pc (
  input  rst,
  input  we,
  input  [31:0] nextpc,
  output [31:0] currentpc
);
endmodule

module regfile (
  input  [4:0] rs1,
  input  [4:0] rs2,
  input  [31:0] write_data,
  input  [4:0] rd,
  output [31:0] rs1_val,
  output [31:0] rs2_val
);
endmodule

module ifid (
  input  we,
  input  flush,
  input  [31:0] pc_in,
  input  [31:0] instr_in,
  output [31:0] pc,
  output [31:0] instr
);
endmodule

module idex (
  input  flush,
  input  [31:0] pc_in,
  input  [31:0] reg1_in,
  input  [31:0] reg2_in,
  input  [31:0] imm_in,
  input  alu_in1_sel_in,
  input  alu_in2_sel_in,
  input  [2:0] alu_op_in,
  input  alu_mod_in,
  input  [2:0] funct3_in,
  input  is_cond_in,
  input  nextpc_sel_in,
  input  mem_mode_in,
  input  [1:0] rf_in_sel_in,
  input  [4:0] rwrite_in,
  output [31:0] pc,
  output [31:0] reg1,
  output [31:0] reg2,
  output [31:0] imm,
  output alu_in1_sel,
  output alu_in2_sel,
  output [2:0] alu_op,
  output alu_mod,
  output [2:0] funct3,
  output is_cond,
  output nextpc_sel,
  output mem_mode,
  output [1:0] rf_in_sel,
  output [4:0] rwrite
);
endmodule

module compare (
  input  [31:0] a,
  input  [31:0] b,
  input  [2:0] funct3,
  output result
);
endmodule

module exmem (
  input  [31:0] pcplus4_in,
  input  [31:0] alu_out_in,
  input  [31:0] reg2_in,
  input  [2:0] funct3_in,
  input  mem_mode_in,
  input  [1:0] rf_in_sel_in,
  input  [4:0] rwrite_in,
  output [31:0] pcplus4,
  output [31:0] alu_out,
  output [31:0] reg2,
  output [2:0] funct3,
  output mem_mode,
  output [1:0] rf_in_sel,
  output [4:0] rwrite
);
endmodule

module memwb (
  input  [31:0] pcplus4_in,
  input  [31:0] alu_out_in,
  input  [31:0] mem_out_in,
  input  [1:0] rf_in_sel_in,
  input  [4:0] rwrite_in,
  output [31:0] pcplus4,
  output [31:0] alu_out,
  output [31:0] mem_out,
  output [1:0] rf_in_sel,
  output [4:0] rwrite
);
endmodule

module forwarding (
  input  rs1_ex,
  input  rs2_ex,
  input  rd_mem,
  input  rf_in_sel_mem,
  input  rd_wb,
  input  rf_in_sel_wb,
  output [1:0] forward_rs1,
  output [1:0] forward_rs2
);
endmodule

module hazard (
  input  [4:0] rs1_id,
  input  [4:0] rs2_id,
  input  [4:0] rd_ex,
  input  [1:0] rf_in_sel_ex,
  input  nextpc_sel_ex_cond,
  output if_id_we,
  output if_id_flush,
  output id_ex_flush,
  output pc_we
);
endmodule
